# Fritzing sketch circuit (saved by Fritzing 0.9.3b)
breadboards: 1

parts:
  Part1 = Arduino Mega 2560 (Rev3)
  Part2 = Thumb Joystick
  Part3 = Thumb Joystick
  LCD2 = LCD screen
  R3 = Resistor [tolerance=±5% resistance=10k package="0603 [SMD]"]

nets:
  N1: Part1.A0, Part3.HORZ
  N2: Part1.A1, Part3.VERT
  N3: Part1.A2, Part2.VERT
  N4: Part1.A3, Part2.HORZ
  VCC: Part1.5V, Part2.VCC, Part3.VCC, LCD2.LED+
  GND: Part1.GND, Part2.GND, Part3.GND, LCD2.VSS, LCD2.LED-
  N5: Part1.D23, LCD2.DB7
  N6: Part1.D25, LCD2.DB6
  N7: Part1.D27, LCD2.DB5
  N8: Part1.D29, LCD2.DB4
  N9: Part1.D31, LCD2.E, LCD2.DB0
  N10: Part1.D33, LCD2.RS
  N11: LCD2.VDD, LCD2.V0, R3.Pin_1
  N12: LCD2.R/W, R3.Pin_0
